// Digital circuit alu.dig as structural Verilog
module alu (
  input  [15:0] data_right,
  input  [15:0] data_left,
  input  [3:0] alu_op,
  output [3:0] flags,
  output [15:0] res
);

  Add #(.Bits(16)) add_1 (.a(data_left), .b(data_right), .c_i(1'b0), .s(res));  // open: c_o
  barrel_shifter barrel_shifter_1 ();  // open: n, asr, shl, in, out

  assign flags = 4'b0000;
endmodule
