// Digital circuit cpu.dig as structural Verilog
module cpu (
);

  wire clk, decode_1_p3, decode_1_p4, decode_1_p5, jmp_en;
  wire [1:0] w_ram, wb_sel;
  wire [2:0] cond;
  wire [3:0] alu_1_flags, decode_1_p6, decode_1_p7, decode_1_p11;
  wire [15:0] decode_1_p8, fetch_1_inst, memory_1_q, pc, regfile_1_data_left, regfile_1_data_right,
       regfile_1_data_src, res, writeback_1_data_wb;

  Button u_clk (.out(clk));
  fetch fetch_1 (.jmp_en(jmp_en), .dst(res), .clk(clk), .pc(pc), .inst(fetch_1_inst));
  // Probe on pc
  // decode decode_1: pin names not known; wires that end beside it: fetch_1_inst, cond, decode_1_p3, decode_1_p4, decode_1_p5, decode_1_p6, decode_1_p7, decode_1_p8, w_ram, wb_sel, decode_1_p11
  regfile regfile_1 (
    .data_in(writeback_1_data_wb), .clk(clk), .pc(pc), .write_en(decode_1_p3), .left_sel(decode_1_p4),
    .right_sel(decode_1_p5), .reg_src(decode_1_p6), .reg_dst(decode_1_p7), .imm(decode_1_p8),
    .data_left(regfile_1_data_left), .data_right(regfile_1_data_right), .data_src(regfile_1_data_src));
  // Probe left on regfile_1_data_left
  // Probe right on regfile_1_data_right
  alu alu_1 (
    .data_right(regfile_1_data_left), .data_left(regfile_1_data_right), .op(decode_1_p11), .clk(clk),
    .flags(alu_1_flags), .res(res));
  jump_unit jump_unit_1 (.flags(alu_1_flags), .cond(cond), .jmp_en(jmp_en));
  // Probe wb on writeback_1_data_wb
  memory memory_1 (.addr(res), .data(regfile_1_data_src), .we(w_ram), .q(memory_1_q));
  writeback writeback_1 (.alu(res), .mem(memory_1_q), .pc(pc), .wb_sel(wb_sel), .data_wb(writeback_1_data_wb));
endmodule
