// Digital circuit decode.dig as structural Verilog
module decode (
  input  [15:0] instr,
  output [2:0] cond,
  output write_reg,
  output left_sel,
  output right_sel,
  output [3:0] reg_src,
  output [3:0] reg_dst,
  output [15:0] imm,
  output [3:0] alu_op,
  output write_ram,
  output [1:0] wb_sel
);


  assign alu_op = 4'b0000;
  assign cond = 3'b000;
  assign imm = {16{1'b0}};
  assign left_sel = 1'b0;
  assign reg_dst = 4'b0000;
  assign reg_src = 4'b0000;
  assign right_sel = 1'b0;
  assign wb_sel = 2'b00;
  assign write_ram = 1'b0;
  assign write_reg = 1'b0;

  // Other names for the same wires on the sheet: b0 = instr[0]; b1 = instr[1]; b2 = instr[2]; b3 = instr[3];
  //   b4 = instr[4]; b5 = instr[5]; b6 = instr[6]; b7 = instr[7]; b8 = instr[8]; b9 = instr[9]; b10 = instr[10];
  //   b11 = instr[11]; b12 = instr[12]; b13 = instr[13]; b14 = instr[14]; b15 = instr[15]
endmodule
